# Fritzing sketch origin-I (saved by Fritzing 0.9.3b)
breadboards: 1

parts:
  Part1 = Adafruit Feather M0 Bluefruit LE [part_number="Adafruit #2995"]
  Part2 = Adafruit DRV2605L [part_number="Adafruit #2305"]
  Part3 = Adafruit VL53L0X Time of Flight Distance Sensor [part_number="Adafruit #3317"]
  Part4 = Adafruit LSM9DS1 9DoF Breakout [part_number="Adafruit #3387"]
  Part5 = 16 NeoPixel Ring [part_number=1463]

nets:
  GND: Part1.GND, Part2.GND, Part3.GND, Part4.GND, Part5.GND
  VIN: Part1.+3V3, Part2.VIN, Part3.VIN, Part4.VIN, Part5.VDD
  N1: Part1.D6, Part5.IN
  N2: Part1.SCL, Part2.SCL, Part3.SCL, Part4.SCL
  N3: Part1.SDA, Part2.SDA, Part3.SDA, Part4.SDA

custom parts:
  Adafruit Feather M0 Bluefruit LE: This is the Adafruit Feather M0 Bluefruit LE - our take on an 'all-in-one' Arduino-compatible + Bluetooth Low Energy with built in USB and battery charging. Its an Adafruit Feather M0 with a BTLE module, ready to rock! We have other boards in the Feather family, check'em out here. Bluetooth Low Energy is the hottest new low-power, 2.4GHz spectrum wireless protocol. In particular, its the only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
  Adafruit DRV2605L: The DRV2605 from TI is a fancy little motor driver. Rather than controlling a stepper motor or DC motor, its designed specifically for controlling haptic motors - buzzers and vibration motors. Normally one would just turn those kinds of motors on and off, but this driver has the ability to have various effects when driving a vibe motor. For example, ramping the vibration level up and down,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
  Adafruit VL53L0X Time of Flight Distance Sensor: The VL53L0X is a Time of Flight distance sensor like no other you've used! The sensor contains a very tiny invisible laser source, and a matching sensor. The VL53L0X can detect the "time of flight", or how long the light has taken to bounce back to the sensor. Since it uses a very narrow light source, it is good for determining distance of only the surface directly in front of it. Unlike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
  Adafruit LSM9DS1 9DoF Breakout: Add motion, direction and orientation sensing to your Arduino project with this all-in-one 9-DOF sensor. Inside the chip are three sensors, one is a classic 3-axis accelerometer, which can tell you which direction is down towards the Earth (by measuring gravity) or how fast the board is accelerating in 3D space. The other is a 3-axis magnetometer that can sense where the strongest magnetic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
  16 NeoPixel Ring: 16 ultra bright smart LED NeoPixels are arranged in a circle with 1.75" (44.5mm) outer diameter. The rings are 'chainable' - connect the output pin of one to the input pin of another. Use only one microcontroller pin to control as many as you can chain together! Each LED is addressable as the driver chip is inside the LED. Each one has ~18mA constant current drive so the color will be very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
